// Logisim project seq_circuit.circ as structural Verilog: 1 circuit, main circuit main
module main (
  input  in_1,
  input  in_2,
  output out_3
);

  wire and_1_out, and_2_out, d_ff_1_q, d_ff_1_qn, or_1_out, undriven, xor_1_out;

  xor xor_1 (xor_1_out, in_1, in_2);
  and and_1 (and_1_out, in_1, in_2);
  xor xor_2 (out_3, xor_1_out, d_ff_1_qn);
  and and_2 (and_2_out, xor_1_out, d_ff_1_qn);
  Clock clock_1 ();  // open: out
  or or_1 (or_1_out, and_2_out, and_1_out);
  D_Flip_Flop d_ff_1 (.clk(undriven), .D(or_1_out), .Q(d_ff_1_q), .Qn(d_ff_1_qn));  // open: preset, en, reset
endmodule
